// Logisim project single_register.circ as structural Verilog: 1 circuit, main circuit main
module main (
  input  [63:0] HIGH_DATA0,
  input  [63:0] LOW_DATA0,
  input  [63:0] HIGH_DATA1,
  input  [63:0] LOW_DATA1,
  input  [3:0] CTX_STORE_SELECT,
  input  [3:0] CTX_LOAD_SELECT,
  input  CTX_STORE,
  input  CTX_LOAD,
  input  BUS_IN_SELECT,
  input  BUS_OUT_SELECT,
  input  OUTPUT_ENABLE,
  input  WRITE_ENABLE,
  input  CLOCK,
  output [63:0] HIGH_DATA_OUT0,
  output [63:0] LOW_DATA_OUT0,
  output [63:0] HIGH_DATA_OUT1,
  output [63:0] LOW_DATA_OUT1
);

  wire demultiplexer_3_out0, demultiplexer_3_out1, demultiplexer_4_out0, demultiplexer_4_out1,
       demultiplexer_4_out2, demultiplexer_4_out3, demultiplexer_4_out4, demultiplexer_4_out5,
       demultiplexer_4_out6, demultiplexer_4_out7, demultiplexer_4_out8, demultiplexer_4_out9,
       demultiplexer_4_out10, demultiplexer_4_out11, demultiplexer_4_out12, demultiplexer_4_out13,
       demultiplexer_4_out14, demultiplexer_4_out15, demultiplexer_5_out0, demultiplexer_5_out1,
       demultiplexer_5_out2, demultiplexer_5_out3, demultiplexer_5_out4, demultiplexer_5_out5,
       demultiplexer_5_out6, demultiplexer_5_out7, demultiplexer_5_out8, demultiplexer_5_out9,
       demultiplexer_5_out10, demultiplexer_5_out11, demultiplexer_5_out12, demultiplexer_5_out13,
       demultiplexer_5_out14, demultiplexer_5_out15, or_1_out, or_2_out;
  wire [63:0] controlled_buffer_1_out, controlled_buffer_2_out, demultiplexer_1_out0, demultiplexer_1_out1,
       demultiplexer_2_out0, demultiplexer_2_out1, HIGH_q, LOW_q, multiplexer_1_out, multiplexer_2_out,
       register_1_q, register_2_q, register_3_q, register_4_q, register_5_q, register_6_q, register_7_q,
       register_8_q, register_9_q, register_10_q, register_11_q, register_12_q, register_13_q, register_14_q,
       register_15_q, register_16_q, register_17_q, register_18_q, register_19_q, register_20_q,
       register_21_q, register_22_q, register_23_q, register_24_q, register_25_q, register_26_q,
       register_27_q, register_28_q, register_29_q, register_30_q, register_31_q, register_32_q;

  Register #(.width(64)) register_1 (.D(HIGH_q), .en(demultiplexer_5_out3), .clk(CLOCK), .Q(register_1_q), .clr(1'b0));
  Register #(.width(64)) register_2 (.D(LOW_q), .en(demultiplexer_5_out3), .clk(CLOCK), .Q(register_2_q), .clr(1'b0));
  Register #(.width(64)) register_3 (.D(HIGH_q), .en(demultiplexer_5_out2), .clk(CLOCK), .Q(register_3_q), .clr(1'b0));
  Register #(.width(64)) register_4 (.D(LOW_q), .en(demultiplexer_5_out2), .clk(CLOCK), .Q(register_4_q), .clr(1'b0));
  Register #(.width(64)) register_5 (.D(HIGH_q), .en(demultiplexer_5_out1), .clk(CLOCK), .Q(register_5_q), .clr(1'b0));
  Register #(.width(64)) register_6 (.D(LOW_q), .en(demultiplexer_5_out1), .clk(CLOCK), .Q(register_6_q), .clr(1'b0));
  Register #(.width(64)) register_7 (.D(HIGH_q), .en(demultiplexer_5_out0), .clk(CLOCK), .Q(register_7_q), .clr(1'b0));
  Register #(.width(64)) register_8 (.D(LOW_q), .en(demultiplexer_5_out0), .clk(CLOCK), .Q(register_8_q), .clr(1'b0));
  assign controlled_buffer_1_out = demultiplexer_4_out3 ? register_1_q : 64'bz;  // Controlled_Buffer controlled_buffer_1
  assign controlled_buffer_2_out = demultiplexer_4_out3 ? register_2_q : 64'bz;  // Controlled_Buffer controlled_buffer_2
  assign controlled_buffer_1_out = demultiplexer_4_out2 ? register_3_q : 64'bz;  // Controlled_Buffer controlled_buffer_3
  assign controlled_buffer_2_out = demultiplexer_4_out2 ? register_4_q : 64'bz;  // Controlled_Buffer controlled_buffer_4
  assign controlled_buffer_1_out = demultiplexer_4_out1 ? register_5_q : 64'bz;  // Controlled_Buffer controlled_buffer_5
  assign controlled_buffer_2_out = demultiplexer_4_out1 ? register_6_q : 64'bz;  // Controlled_Buffer controlled_buffer_6
  assign controlled_buffer_1_out = demultiplexer_4_out0 ? register_7_q : 64'bz;  // Controlled_Buffer controlled_buffer_7
  assign controlled_buffer_2_out = demultiplexer_4_out0 ? register_8_q : 64'bz;  // Controlled_Buffer controlled_buffer_8
  // NOT_Gate not_1 is placed but not wired
  Register #(.width(64)) register_9 (.D(HIGH_q), .en(demultiplexer_5_out7), .clk(CLOCK), .Q(register_9_q), .clr(1'b0));
  Register #(.width(64)) register_10 (.D(LOW_q), .en(demultiplexer_5_out7), .clk(CLOCK), .Q(register_10_q), .clr(1'b0));
  Register #(.width(64)) register_11 (
    .D(HIGH_q), .en(demultiplexer_5_out6), .clk(CLOCK), .Q(register_11_q), .clr(1'b0));
  Register #(.width(64)) register_12 (.D(LOW_q), .en(demultiplexer_5_out6), .clk(CLOCK), .Q(register_12_q), .clr(1'b0));
  Register #(.width(64)) register_13 (
    .D(HIGH_q), .en(demultiplexer_5_out5), .clk(CLOCK), .Q(register_13_q), .clr(1'b0));
  Register #(.width(64)) register_14 (.D(LOW_q), .en(demultiplexer_5_out5), .clk(CLOCK), .Q(register_14_q), .clr(1'b0));
  Register #(.width(64)) register_15 (
    .D(HIGH_q), .en(demultiplexer_5_out4), .clk(CLOCK), .Q(register_15_q), .clr(1'b0));
  Register #(.width(64)) register_16 (.D(LOW_q), .en(demultiplexer_5_out4), .clk(CLOCK), .Q(register_16_q), .clr(1'b0));
  Multiplexer #(.width(64)) multiplexer_1 (
    .in0(HIGH_DATA0), .in1(HIGH_DATA1), .out(multiplexer_1_out), .sel(BUS_IN_SELECT));
  Multiplexer #(.width(64)) multiplexer_2 (
    .in0(LOW_DATA0), .in1(LOW_DATA1), .out(multiplexer_2_out), .sel(BUS_IN_SELECT));
  assign controlled_buffer_1_out = demultiplexer_4_out7 ? register_9_q : 64'bz;  // Controlled_Buffer controlled_buffer_9
  assign controlled_buffer_2_out = demultiplexer_4_out7 ? register_10_q : 64'bz;  // Controlled_Buffer controlled_buffer_10
  assign controlled_buffer_1_out = demultiplexer_4_out6 ? register_11_q : 64'bz;  // Controlled_Buffer controlled_buffer_11
  assign controlled_buffer_2_out = demultiplexer_4_out6 ? register_12_q : 64'bz;  // Controlled_Buffer controlled_buffer_12
  assign controlled_buffer_1_out = demultiplexer_4_out5 ? register_13_q : 64'bz;  // Controlled_Buffer controlled_buffer_13
  assign controlled_buffer_2_out = demultiplexer_4_out5 ? register_14_q : 64'bz;  // Controlled_Buffer controlled_buffer_14
  assign controlled_buffer_1_out = demultiplexer_4_out4 ? register_15_q : 64'bz;  // Controlled_Buffer controlled_buffer_15
  assign controlled_buffer_2_out = demultiplexer_4_out4 ? register_16_q : 64'bz;  // Controlled_Buffer controlled_buffer_16
  assign controlled_buffer_1_out = WRITE_ENABLE ? multiplexer_1_out : 64'bz;  // Controlled_Buffer controlled_buffer_17
  assign controlled_buffer_2_out = WRITE_ENABLE ? multiplexer_2_out : 64'bz;  // Controlled_Buffer controlled_buffer_18
  or or_1 (or_1_out, CTX_LOAD, WRITE_ENABLE);
  Register #(.width(64)) HIGH (.D(controlled_buffer_1_out), .en(or_1_out), .clk(CLOCK), .Q(HIGH_q), .clr(1'b0));
  Register #(.width(64)) LOW (.D(controlled_buffer_2_out), .en(or_1_out), .clk(CLOCK), .Q(LOW_q), .clr(1'b0));
  Register #(.width(64)) register_17 (
    .D(HIGH_q), .en(demultiplexer_5_out11), .clk(CLOCK), .Q(register_17_q), .clr(1'b0));
  Register #(.width(64)) register_18 (
    .D(LOW_q), .en(demultiplexer_5_out11), .clk(CLOCK), .Q(register_18_q), .clr(1'b0));
  Register #(.width(64)) register_19 (
    .D(HIGH_q), .en(demultiplexer_5_out10), .clk(CLOCK), .Q(register_19_q), .clr(1'b0));
  Register #(.width(64)) register_20 (
    .D(LOW_q), .en(demultiplexer_5_out10), .clk(CLOCK), .Q(register_20_q), .clr(1'b0));
  Register #(.width(64)) register_21 (
    .D(HIGH_q), .en(demultiplexer_5_out9), .clk(CLOCK), .Q(register_21_q), .clr(1'b0));
  Register #(.width(64)) register_22 (.D(LOW_q), .en(demultiplexer_5_out9), .clk(CLOCK), .Q(register_22_q), .clr(1'b0));
  Register #(.width(64)) register_23 (
    .D(HIGH_q), .en(demultiplexer_5_out8), .clk(CLOCK), .Q(register_23_q), .clr(1'b0));
  Register #(.width(64)) register_24 (.D(LOW_q), .en(demultiplexer_5_out8), .clk(CLOCK), .Q(register_24_q), .clr(1'b0));
  Demultiplexer #(.width(64)) demultiplexer_1 (
    .out0(demultiplexer_1_out0), .out1(demultiplexer_1_out1), .in(HIGH_q), .sel(BUS_OUT_SELECT));
  Demultiplexer #(.width(64)) demultiplexer_2 (
    .out0(demultiplexer_2_out0), .out1(demultiplexer_2_out1), .in(LOW_q), .sel(BUS_OUT_SELECT));
  or or_2 (or_2_out, BUS_OUT_SELECT, OUTPUT_ENABLE);
  Demultiplexer demultiplexer_3 (
    .out0(demultiplexer_3_out0), .out1(demultiplexer_3_out1), .in(or_2_out), .sel(OUTPUT_ENABLE));
  Demultiplexer #(.select(4)) demultiplexer_4 (
    .out0(demultiplexer_4_out0), .out1(demultiplexer_4_out1), .out2(demultiplexer_4_out2),
    .out3(demultiplexer_4_out3), .out4(demultiplexer_4_out4), .out5(demultiplexer_4_out5),
    .out6(demultiplexer_4_out6), .out7(demultiplexer_4_out7), .out8(demultiplexer_4_out8),
    .out9(demultiplexer_4_out9), .out10(demultiplexer_4_out10), .out11(demultiplexer_4_out11),
    .out12(demultiplexer_4_out12), .out13(demultiplexer_4_out13), .out14(demultiplexer_4_out14),
    .out15(demultiplexer_4_out15), .in(CTX_LOAD), .sel(CTX_LOAD_SELECT));
  assign controlled_buffer_1_out = demultiplexer_4_out11 ? register_17_q : 64'bz;  // Controlled_Buffer controlled_buffer_19
  assign controlled_buffer_2_out = demultiplexer_4_out11 ? register_18_q : 64'bz;  // Controlled_Buffer controlled_buffer_20
  assign controlled_buffer_1_out = demultiplexer_4_out10 ? register_19_q : 64'bz;  // Controlled_Buffer controlled_buffer_21
  assign controlled_buffer_2_out = demultiplexer_4_out10 ? register_20_q : 64'bz;  // Controlled_Buffer controlled_buffer_22
  assign controlled_buffer_1_out = demultiplexer_4_out9 ? register_21_q : 64'bz;  // Controlled_Buffer controlled_buffer_23
  assign controlled_buffer_2_out = demultiplexer_4_out9 ? register_22_q : 64'bz;  // Controlled_Buffer controlled_buffer_24
  assign controlled_buffer_1_out = demultiplexer_4_out8 ? register_23_q : 64'bz;  // Controlled_Buffer controlled_buffer_25
  assign controlled_buffer_2_out = demultiplexer_4_out8 ? register_24_q : 64'bz;  // Controlled_Buffer controlled_buffer_26
  assign HIGH_DATA_OUT0 = demultiplexer_3_out1 ? demultiplexer_1_out0 : 64'bz;  // Controlled_Buffer controlled_buffer_27
  assign LOW_DATA_OUT0 = demultiplexer_3_out1 ? demultiplexer_2_out0 : 64'bz;  // Controlled_Buffer controlled_buffer_28
  assign HIGH_DATA_OUT1 = demultiplexer_3_out0 ? demultiplexer_1_out1 : 64'bz;  // Controlled_Buffer controlled_buffer_29
  assign LOW_DATA_OUT1 = demultiplexer_3_out0 ? demultiplexer_2_out1 : 64'bz;  // Controlled_Buffer controlled_buffer_30
  Demultiplexer #(.select(4)) demultiplexer_5 (
    .out0(demultiplexer_5_out0), .out1(demultiplexer_5_out1), .out2(demultiplexer_5_out2),
    .out3(demultiplexer_5_out3), .out4(demultiplexer_5_out4), .out5(demultiplexer_5_out5),
    .out6(demultiplexer_5_out6), .out7(demultiplexer_5_out7), .out8(demultiplexer_5_out8),
    .out9(demultiplexer_5_out9), .out10(demultiplexer_5_out10), .out11(demultiplexer_5_out11),
    .out12(demultiplexer_5_out12), .out13(demultiplexer_5_out13), .out14(demultiplexer_5_out14),
    .out15(demultiplexer_5_out15), .in(CTX_STORE), .sel(CTX_STORE_SELECT));
  Register #(.width(64)) register_25 (
    .D(HIGH_q), .en(demultiplexer_5_out15), .clk(CLOCK), .Q(register_25_q), .clr(1'b0));
  Register #(.width(64)) register_26 (
    .D(LOW_q), .en(demultiplexer_5_out15), .clk(CLOCK), .Q(register_26_q), .clr(1'b0));
  Register #(.width(64)) register_27 (
    .D(HIGH_q), .en(demultiplexer_5_out14), .clk(CLOCK), .Q(register_27_q), .clr(1'b0));
  Register #(.width(64)) register_28 (
    .D(LOW_q), .en(demultiplexer_5_out14), .clk(CLOCK), .Q(register_28_q), .clr(1'b0));
  Register #(.width(64)) register_29 (
    .D(HIGH_q), .en(demultiplexer_5_out13), .clk(CLOCK), .Q(register_29_q), .clr(1'b0));
  Register #(.width(64)) register_30 (
    .D(LOW_q), .en(demultiplexer_5_out13), .clk(CLOCK), .Q(register_30_q), .clr(1'b0));
  Register #(.width(64)) register_31 (
    .D(HIGH_q), .en(demultiplexer_5_out12), .clk(CLOCK), .Q(register_31_q), .clr(1'b0));
  Register #(.width(64)) register_32 (
    .D(LOW_q), .en(demultiplexer_5_out12), .clk(CLOCK), .Q(register_32_q), .clr(1'b0));
  assign controlled_buffer_1_out = demultiplexer_4_out15 ? register_25_q : 64'bz;  // Controlled_Buffer controlled_buffer_31
  assign controlled_buffer_2_out = demultiplexer_4_out15 ? register_26_q : 64'bz;  // Controlled_Buffer controlled_buffer_32
  assign controlled_buffer_1_out = demultiplexer_4_out14 ? register_27_q : 64'bz;  // Controlled_Buffer controlled_buffer_33
  assign controlled_buffer_2_out = demultiplexer_4_out14 ? register_28_q : 64'bz;  // Controlled_Buffer controlled_buffer_34
  assign controlled_buffer_1_out = demultiplexer_4_out13 ? register_29_q : 64'bz;  // Controlled_Buffer controlled_buffer_35
  assign controlled_buffer_2_out = demultiplexer_4_out13 ? register_30_q : 64'bz;  // Controlled_Buffer controlled_buffer_36
  assign controlled_buffer_1_out = demultiplexer_4_out12 ? register_31_q : 64'bz;  // Controlled_Buffer controlled_buffer_37
  assign controlled_buffer_2_out = demultiplexer_4_out12 ? register_32_q : 64'bz;  // Controlled_Buffer controlled_buffer_38
endmodule
